# Fritzing sketch colakic (saved by Fritzing 0.9.3b)
breadboards: 1

parts:
  Part1 = Arduino Uno (Rev3)
  J2 = Basic Servo
  J1 = Basic Servo
  Part2 = Thumb Joystick

nets:
  N1: Part1.D1/TX, J2.pulse
  VCC: Part1.5V, J1.vcc, Part2.VCC
  GND: Part1.GND, J2.gnd, J1.gnd, Part2.GND
